# Fritzing sketch alps-arduino (saved by Fritzing 0.9.6b)
breadboards: 1

parts:
  Part1 = Arduino Mega ADK (Rev3)
  Part2 = Bluetooth HC-05 Macho
  R2 = Resistor [tolerance=±5% power=0.25 resistance=300 package=THT]
  NEOPIXEL2 = Neopixel Strip -- Black (30/m)
  USBTTL2 = USB A Plug
  C2 = Electrolytic Capacitor [capacitance=500µF voltage=35V package="100 mil [THT, electrolytic]"]
  USBTTL3 = Micro USB B Plug
  R3 = Resistor [tolerance=±5% resistance=1k package="0805 [SMD]"]
  R4 = Resistor [tolerance=±5% resistance=2k package="2010 [SMD]"]

nets:
  N1: Part1.D15/RX3, Part2.TXD
  N2: Part1.D14/TX3, R3.Pin_1
  GND: Part1.GND, Part2.GND, NEOPIXEL2.GND, USBTTL2.gnd, C2.-, USBTTL3.gnd, R4.Pin_1
  N3: Part1.D8_PWM, R2.Pin_1
  N4: Part2.RXD, R3.Pin_0, R4.Pin_0
  +5V: Part2.VCC, NEOPIXEL2.+5V, USBTTL2.5v, C2.+, USBTTL3.+5v
  N5: R2.Pin_0, NEOPIXEL2.DI

custom parts:
  Neopixel Strip -- Black (30/m): Neopixel Strip, Black, 30 pixels per meter.
