# Fritzing sketch alps-teensy (saved by Fritzing 0.9.6b)
breadboards: 1

parts:
  U1 = 74AHCT125 [part_number=SN74AHCT125 package=dil14]
  Teensy1 = Teensy 4.0
  Part1 = Bluetooth HC-05 Macho
  C1 = Electrolytic Capacitor [capacitance=500µF voltage=35V package="100 mil [THT, electrolytic]"]
  R1 = Resistor [tolerance=±5% power=0.25 resistance=300 package=THT]
  NEOPIXEL1 = Neopixel Strip -- Black (30/m)
  USBTTL1 = USB A Plug

nets:
  GND: U1.1OE, U1.2OE, U1.GND, U1.3OE, U1.4OE, Teensy1.pin_1, Teensy1.pin_17, Teensy1.pin_32, Part1.GND, C1.-, NEOPIXEL1.GND, USBTTL1.gnd
  N1: U1.1A, Teensy1.pin_10
  N2: U1.1Y, R1.Pin_0
  VCC: U1.VCC, Teensy1.pin33, Part1.VCC, C1.+, NEOPIXEL1.+5V, USBTTL1.5v
  N3: Teensy1.pin_21, Part1.RXD
  N4: Teensy1.pin_22, Part1.TXD
  N5: R1.Pin_1, NEOPIXEL1.DI

custom parts:
  74AHCT125: Quad Level-Shifter (3V to 5V) Quadruple Bus Buffer Gates With 3-State Outputs
  Teensy 4.0: The Teensy is a complete USB-based microcontoller development system, in a very small footprint, capable of implementing many types of projects. All programming is done via the USB port. No special programmer is needed, only a standard micro-USB cable and a PC or Macintosh with a USB port.
  Neopixel Strip -- Black (30/m): Neopixel Strip, Black, 30 pixels per meter.
